// Logisim project final.circ as structural Verilog: 3 circuits, main circuit Dispenser
module track (
  input  [2:0] USER_ID,
  input  reset,
  input  clk,
  output [15:0] visits
);

  wire decoder_1_out0, decoder_1_out1, decoder_1_out2, decoder_1_out3, decoder_1_out4, decoder_1_out5,
       decoder_1_out6, decoder_1_out7;
  wire [15:0] adder_1_out, U0_q, U1_q, U2_q, U3_q, U4_q, U5_q, U6_q, U7_q;

  Decoder #(.select(3)) decoder_1 (
    .out0(decoder_1_out0), .out1(decoder_1_out1), .out2(decoder_1_out2), .out3(decoder_1_out3),
    .out4(decoder_1_out4), .out5(decoder_1_out5), .out6(decoder_1_out6), .out7(decoder_1_out7),
    .sel(USER_ID), .en(1'b1));
  Register #(.width(16)) U0 (.D(adder_1_out), .en(decoder_1_out0), .Q(U0_q), .clk(clk), .clr(reset));
  Register #(.width(16)) U1 (.D(adder_1_out), .en(decoder_1_out1), .Q(U1_q), .clk(clk), .clr(reset));
  Register #(.width(16)) U2 (.D(adder_1_out), .en(decoder_1_out2), .Q(U2_q), .clk(clk), .clr(reset));
  Register #(.width(16)) U3 (.D(adder_1_out), .en(decoder_1_out3), .Q(U3_q), .clk(clk), .clr(reset));
  Register #(.width(16)) U4 (.D(adder_1_out), .en(decoder_1_out4), .Q(U4_q), .clk(clk), .clr(reset));
  Register #(.width(16)) U5 (.D(adder_1_out), .en(decoder_1_out5), .Q(U5_q), .clk(clk), .clr(reset));
  Register #(.width(16)) U6 (.D(adder_1_out), .en(decoder_1_out6), .Q(U6_q), .clk(clk), .clr(reset));
  Register #(.width(16)) U7 (.D(adder_1_out), .en(decoder_1_out7), .Q(U7_q), .clk(clk), .clr(reset));
  Multiplexer #(.select(3), .width(16)) multiplexer_1 (
    .in0(U0_q), .in1(U1_q), .in2(U2_q), .in3(U3_q), .in4(U4_q), .in5(U5_q), .in6(U6_q), .in7(U7_q),
    .out(visits), .sel(USER_ID), .en(1'b1));
  Adder #(.width(16)) adder_1 (.a(visits), .b(16'h1), .out(adder_1_out));  // open: cin, cout
endmodule

// Status
module Dispenser (
  input  [15:0] init_water_stock,
  input  [15:0] init_juice_stock,
  input  [15:0] init_soda_stock,
  input  [15:0] WFR,
  input  [15:0] JFR,
  input  [15:0] SFR,
  input  [15:0] WNR,
  input  [1:0] fluid_type,
  input  reset,
  input  [15:0] JNR,
  input  CLK,
  input  [15:0] SNR,
  input  [2:0] user,
  input  [15:0] volume_units,
  output [15:0] original,
  output [15:0] discount,
  output [15:0] remaining_qty,
  output [15:0] final_price
);

  wire comparator_1_gt, comparator_2_eq, comparator_2_gt, decoder_1_out0, decoder_1_out1, decoder_1_out2,
       nand_1_out, nand_2_out, nand_3_out, not_1_out, or_1_out;
  wire [15:0] demultiplexer_1_out0, demultiplexer_1_out1, demultiplexer_1_out2, multiplexer_1_out,
       multiplexer_2_out, multiplexer_3_out, multiplexer_4_out, multiplexer_5_out, multiplexer_6_out,
       multiplexer_7_out, multiplexer_8_out, multiplexer_9_out, multiplexer_10_out, multiplier_1_out,
       register_1_q, register_2_q, register_3_q, subtractor_1_out, subtractor_2_out, track_1_visits;

  Multiplexer #(.select(2), .width(16)) multiplexer_1 (
    .in0(register_2_q), .in1(register_3_q), .in2(register_1_q), .in3({16{1'b0}}), .out(multiplexer_1_out),
    .sel(fluid_type));  // open: en
  not not_1 (not_1_out, reset);
  Comparator #(.width(16), .mode("unsigned")) comparator_1 (
    .a(volume_units), .b(multiplexer_1_out), .gt(comparator_1_gt));  // open: eq, lt
  Decoder #(.select(2)) decoder_1 (
    .out0(decoder_1_out0), .out1(decoder_1_out1), .out2(decoder_1_out2), .sel(fluid_type), .en(1'b1));  // open: out3
  Register #(.width(16)) register_1 (
    .D(multiplexer_9_out), .en(decoder_1_out2), .Q(register_1_q), .clk(CLK));  // open: clr
  Multiplexer #(.select(2), .width(16)) multiplexer_2 (
    .in0(WFR), .in1(JFR), .in2(SFR), .in3({16{1'b0}}), .out(multiplexer_2_out), .sel(fluid_type), .en(1'b1));
  Register #(.width(16)) register_2 (
    .D(multiplexer_7_out), .en(decoder_1_out0), .Q(register_2_q), .clk(CLK));  // open: clr
  Register #(.width(16)) register_3 (
    .D(multiplexer_8_out), .en(decoder_1_out1), .Q(register_3_q), .clk(CLK));  // open: clr
  Multiplexer #(.width(16)) multiplexer_3 (
    .in0(init_water_stock), .in1(demultiplexer_1_out0), .out(multiplexer_3_out), .sel(not_1_out), .en(1'b1));
  Multiplexer #(.width(16)) multiplexer_4 (
    .in0(init_juice_stock), .in1(demultiplexer_1_out1), .out(multiplexer_4_out), .sel(not_1_out), .en(1'b1));
  Multiplexer #(.width(16)) multiplexer_5 (
    .in0(init_soda_stock), .in1(demultiplexer_1_out2), .out(multiplexer_5_out), .sel(not_1_out), .en(1'b1));
  Multiplexer #(.select(2), .width(16)) multiplexer_6 (
    .in0(WNR), .in1(JNR), .in2(SNR), .in3({16{1'b0}}), .out(multiplexer_6_out), .sel(fluid_type), .en(1'b1));
  Multiplexer #(.width(16)) multiplexer_7 (
    .in0(multiplexer_3_out), .in1(register_2_q), .out(multiplexer_7_out), .sel(nand_3_out), .en(1'b1));
  Multiplexer #(.width(16)) multiplexer_8 (
    .in0(multiplexer_4_out), .in1(register_3_q), .out(multiplexer_8_out), .sel(nand_2_out), .en(1'b1));
  Multiplexer #(.width(16)) multiplexer_9 (
    .in0(multiplexer_5_out), .in1(register_1_q), .out(multiplexer_9_out), .sel(nand_1_out), .en(1'b1));
  nand nand_1 (nand_1_out, decoder_1_out2, or_1_out);
  Subtractor #(.width(16)) subtractor_1 (.a(volume_units), .b(16'h1), .out(subtractor_1_out));  // open: bin, bout
  nand nand_2 (nand_2_out, decoder_1_out1, or_1_out);
  Multiplexer #(.select(2), .width(16)) multiplexer_10 (
    .in0(register_2_q), .in1(register_3_q), .in2(register_1_q), .in3({16{1'b0}}), .out(multiplexer_10_out),
    .sel(fluid_type), .en(1'b1));
  Multiplier #(.width(16)) multiplier_1 (
    .a(subtractor_1_out), .b(multiplexer_6_out), .out(multiplier_1_out));  // open: cin, cout
  nand nand_3 (nand_3_out, or_1_out, decoder_1_out0);
  Subtractor #(.width(16)) subtractor_2 (
    .a(multiplexer_10_out), .b(volume_units), .out(subtractor_2_out));  // open: bin, bout
  Adder #(.width(16)) adder_1 (.a(multiplexer_2_out), .b(multiplier_1_out), .out(original));  // open: cin, cout
  Demultiplexer #(.select(2), .width(16)) demultiplexer_1 (
    .out0(demultiplexer_1_out0), .out1(demultiplexer_1_out1), .out2(demultiplexer_1_out2),
    .out3(demultiplexer_1_out2), .in(subtractor_2_out), .sel(fluid_type));  // open: en
  Comparator #(.width(16), .mode("unsigned")) comparator_2 (
    .a(multiplexer_10_out), .b(volume_units), .gt(comparator_2_gt), .eq(comparator_2_eq));  // open: lt
  track track_1 (.USER_ID(user), .clk(CLK), .visits(track_1_visits), .reset(reset));
  or or_1 (or_1_out, comparator_2_gt, comparator_2_eq);
  Multiplexer #(.select(2), .width(16)) multiplexer_11 (
    .in0(register_2_q), .in1(register_3_q), .in2(register_1_q), .out(remaining_qty), .sel(fluid_type));  // open: in3, en
  discount discount_1 (.original_price(original), .in_2(track_1_visits), .finalprice(final_price), .discount(discount));
  LED restock (.in(comparator_1_gt));
endmodule

module discount (
  input  [15:0] original_price,
  input  [15:0] in_2,
  output [15:0] discount,
  output [15:0] finalprice
);

  wire and_1_out, comparator_1_eq, comparator_1_gt, comparator_1_lt, comparator_2_eq, comparator_2_gt,
       comparator_2_lt, or_1_out, or_2_out;
  wire [15:0] divider_1_out, multiplexer_1_out, multiplexer_2_out, multiplexer_3_out, multiplier_1_cout,
       multiplier_1_out;

  Comparator #(.width(16)) comparator_1 (
    .a(in_2), .b(16'h2), .gt(comparator_1_gt), .eq(comparator_1_eq), .lt(comparator_1_lt));
  Comparator #(.width(16)) comparator_2 (
    .a(in_2), .b(16'h4), .gt(comparator_2_gt), .eq(comparator_2_eq), .lt(comparator_2_lt));
  or or_1 (or_1_out, comparator_1_eq, comparator_1_lt);
  or or_2 (or_2_out, comparator_2_eq, comparator_2_lt);
  Multiplexer #(.width(16)) multiplexer_1 (
    .in0({16{1'b0}}), .in1({16{1'b0}}), .out(multiplexer_1_out), .sel(or_1_out));  // open: en
  and and_1 (and_1_out, comparator_1_gt, or_2_out);
  Multiplexer #(.width(16)) multiplexer_2 (
    .in0({16{1'b0}}), .in1(16'ha), .out(multiplexer_2_out), .sel(and_1_out));  // open: en
  Multiplexer #(.width(16)) multiplexer_3 (
    .in0(multiplexer_2_out), .in1(16'h14), .out(multiplexer_3_out), .sel(comparator_2_gt));  // open: en
  assign discount = multiplexer_1_out | multiplexer_3_out;  // OR_Gate or_3, 16 bits wide
  Multiplier #(.width(16)) multiplier_1 (
    .a(original_price), .b(discount), .out(multiplier_1_out), .cout(multiplier_1_cout));  // open: cin
  Divider #(.width(16)) divider_1 (
    .a(multiplier_1_out), .b(16'h64), .out(divider_1_out), .upper(multiplier_1_cout));  // open: rem
  Subtractor #(.width(16)) subtractor_1 (.a(original_price), .b(divider_1_out), .out(finalprice));  // open: bin, bout
endmodule
